# Fritzing sketch DomeDrum (saved by Fritzing 0.7.11b)
breadboards: 1

parts:
  Teensy3 = Teensy 2.0
  J11 = Basic Force Sensing Resistor (FSR) [package=THT]
  J12 = Basic Force Sensing Resistor (FSR) [package=THT]
  J13 = Basic Force Sensing Resistor (FSR) [package=THT]
  J14 = Basic Force Sensing Resistor (FSR) [package=THT]
  J15 = Basic Force Sensing Resistor (FSR) [package=THT]
  J16 = Basic Force Sensing Resistor (FSR) [package=THT]
  J17 = Basic Force Sensing Resistor (FSR) [package=THT]
  J18 = Basic Force Sensing Resistor (FSR) [package=THT]
  J19 = Basic Force Sensing Resistor (FSR) [package=THT]
  J20 = Basic Force Sensing Resistor (FSR) [package=THT]
  R12 = Resistor [tolerance=±5% resistance=10k package=THT]
  R13 = Resistor [tolerance=±5% resistance=10k package=THT]
  R14 = Resistor [tolerance=±5% resistance=10k package=THT]
  R15 = Resistor [tolerance=±5% resistance=10k package=THT]
  R16 = Resistor [tolerance=±5% resistance=10k package=THT]
  R17 = Resistor [tolerance=±5% resistance=10k package=THT]
  R18 = Resistor [tolerance=±5% resistance=10k package=THT]
  R19 = Resistor [tolerance=±5% resistance=10k package=THT]
  R20 = Resistor [tolerance=±5% resistance=10k package=THT]
  R21 = Resistor [tolerance=±5% resistance=10k package=THT]

nets:
  N1: Teensy3.GND, R12.Pin_0, R13.Pin_0, R14.Pin_0, R15.Pin_0, R16.Pin_0, R17.Pin_0, R18.Pin_0, R19.Pin_0, R20.Pin_0, R21.Pin_0
  N2: Teensy3.VCC, J11.pin_0, J12.pin_0, J13.pin_0, J14.pin_0, J15.pin_0, J16.pin_0, J17.pin_0, J18.pin_0, J19.pin_0, J20.pin_0
  N3: Teensy3.D7, J11.pin_1, R12.Pin_1
  N4: Teensy3.B4, J12.pin_1, R13.Pin_1
  N5: Teensy3.B5, J13.pin_1, R14.Pin_1
  N6: Teensy3.B6, J14.pin_1, R15.Pin_1
  N7: Teensy3.F7, J15.pin_1, R16.Pin_1
  N8: Teensy3.F6, J16.pin_1, R17.Pin_1
  N9: Teensy3.F5, J17.pin_1, R18.Pin_1
  N10: Teensy3.F4, J18.pin_1, R19.Pin_1
  N11: Teensy3.F1, J20.pin_1, R20.Pin_1
  N12: Teensy3.F0, J19.pin_1, R21.Pin_1

notes:
  drum
  dome

// code stored in the sketch: AnalogInputFSR.ino
/*
  Analog Input
 Demonstrates analog input by reading an analog sensor on analog pin 0 and
 turning on and off a light emitting diode(LED)  connected to digital pin 13. 
 The amount of time the LED will be on and off depends on
 the value obtained by analogRead(). 
 
 The circuit:
 * Potentiometer attached to analog input 0
 * center pin of the potentiometer to the analog pin
 * one side pin (either one) to ground
 * the other side pin to +5V
 * LED anode (long leg) attached to digital output 13
 * LED cathode (short leg) attached to ground
 
 * Note: because most Arduinos have a built-in LED attached 
 to pin 13 on the board, the LED is optional.
 
 
 Created by David Cuartielles
 modified 30 Aug 2011
 By Tom Igoe
 
 This example code is in the public domain.
 
 http://arduino.cc/en/Tutorial/AnalogInput
 
 */

int sensorPin = 2;    // select the input pin for the potentiometer
int ledPin = 13;      // select the pin for the LED
int sensorValue = 0;  // variable to store the value coming from the sensor

void setup() {
  // declare the ledPin as an OUTPUT:
  pinMode(ledPin, OUTPUT);  
}

void loop() {
  // read the value from the sensor:
  sensorValue = analogRead(sensorPin);    
  // turn the ledPin on
  digitalWrite(ledPin, HIGH);  
  // stop the program for <sensorValue> milliseconds:
  delay(sensorValue);          
  // turn the ledPin off:        
  digitalWrite(ledPin, LOW);   
  // stop the program for for <sensorValue> milliseconds:
  delay(sensorValue);                  
}

// code stored in the sketch: Untitled.ino
/*
  Analog Input
 Demonstrates analog input by reading an analog sensor on analog pin 0 and
 turning on and off a light emitting diode(LED)  connected to digital pin 13. 
 The amount of time the LED will be on and off depends on
 the value obtained by analogRead(). 
 
 The circuit:
 * Potentiometer attached to analog input 0
 * center pin of the potentiometer to the analog pin
 * one side pin (either one) to ground
 * the other side pin to +5V
 * LED anode (long leg) attached to digital output 13
 * LED cathode (short leg) attached to ground
 
 * Note: because most Arduinos have a built-in LED attached 
 to pin 13 on the board, the LED is optional.
 
 
 Created by David Cuartielles
 modified 30 Aug 2011
 By Tom Igoe
 
 This example code is in the public domain.
 
 http://arduino.cc/en/Tutorial/AnalogInput
 
 */

int sensorPin = 2;    // select the input pin for the potentiometer
int ledPin = 13;      // select the pin for the LED
int sensorValue = 0;  // variable to store the value coming from the sensor

void setup() {
  // declare the ledPin as an OUTPUT:
  pinMode(ledPin, OUTPUT);  
}

void loop() {
  // read the value from the sensor:
  sensorValue = analogRead(sensorPin);    
  // turn the ledPin on
  digitalWrite(ledPin, HIGH);  
  // stop the program for <sensorValue> milliseconds:
  delay(sensorValue);          
  // turn the ledPin off:        
  digitalWrite(ledPin, LOW);   
  // stop the program for for <sensorValue> milliseconds:
  delay(sensorValue);                  
}
